# Fritzing sketch Circuit Diagram (saved by Fritzing 0.9.3b)
# 18650 Li-ion Battery: CC-BY Dr Kristofer Chan, King's College London/Remote-research.org

parts:
  M1 = PH meter with sensor in breadboard [package=THT]
  A1 = tds-sensor-meter-v1.0_1
  LCD2004-I2C1 = LCD2004-I2C
  M3 = MT3608 Module
  BAT1 = 18650 Li-ion Battery [package=battery-18650]
  BAT2 = 18650 Li-ion Battery [package=battery-18650]
  S1 = Round Pushbutton
  Part1 = Power Cell LiPo Charger/Booster
  M2 = RioRand LM2596
  U1 = ESP32-38PinWide [part_number=ESP32-38PinWide]
  DS2 = DS18B20 1-Wire Temperature Sensor Probe
  R1 = Resistor [tolerance=±5% resistance=4.7k package="0805 [SMD]"]
  LED1 = smd LED [color="Red (633nm)" package="0805 [SMD]"]
  R2 = Resistor [tolerance=±5% resistance=220 package="0805 [SMD]"]
  LED3 = Super Flux LED blue [color=Blue]
  R3 = Resistor [tolerance=±5% resistance=220 package="0805 [SMD]"]

nets:
  N1: M1.pin1, U1.GPIO39
  N2: M1.pin2, A1.pin2, M2.Pin_3, DS2.VDD, R1.Pin_1
  N3: M1.pin3, A1.pin3, U1.GPIO23, DS2.GND
  N4: A1.pin1, U1.GPIO34
  GND: LCD2004-I2C1.GND, M3.pin4, M2.Pin_4, U1.GND, LED1.cathode, LED3.cathode
  VCC: LCD2004-I2C1.VCC, M3.pin3, U1.VIN, R2.Pin_1
  N5: LCD2004-I2C1.SDA, U1.GPIO22
  N6: LCD2004-I2C1.SCL, U1.GPIO21
  N7: M3.pin1, BAT1.-, BAT2.-, Part1.GND, M2.Pin_2
  N8: M3.pin2, S1.leg0, M2.Pin_1
  N9: BAT1.+, BAT2.+, S1.leg1, Part1.VBATT
  N10: U1.GPIO26, R3.Pin_1
  N11: U1.GPIO27, DS2.DQ, R1.Pin_0
  N12: LED1.anode, R2.Pin_0
  N13: LED3.anode, R3.Pin_0

notes:
  WIFI Indicator
  LCD Display
  18650 Battery Charging Module
  pH Sensor
  Turbidity Sensor
  TDS Sensor
  Waterproof Temperature Sensor
  Power Indicator
  <= Buck Converter
  <= Boost Converter
  <= Switch
  <= 18650 Batteries
  <= ESP32 Microcontroller

custom parts:
  PH meter with sensor in breadboard: DFrobot PH meter (SKU SEN0161)
  : TDS Meter V1.0 Development Board Water Meter Filter Measuring Water Sensor Module.
  LCD2004-I2C: A standard character display with 4x20 characters. Comes in many colors with LCM2004 IIC attached.
  MT3608 Module: MT3608 Boost Converter Module Links: Aerosemi MT3608 2A Step Up Converter datasheet
  18650 Li-ion Battery: 18650 li-ion Battery Standard 18650 battery with interactive connectors Creative Common Attribution 4.0 International (CC-BY 4.0) license. Any use of this part requires attribution of Dr Kristofer Chan, Department of Geography, King's College London. Contact kristofer.chan [at] kcl.ac.uk OR kris [at] remote-research.org for further information.
  ESP32-38PinWide: Generic 38-Pin ESP32 with wide format (only access to one side of pins on a breadboard) based on Stephen Lilley's HiLetgo ESP-WROOM-32 ESP32 ESP-32S Development Board.
